// Digital circuit cpu.dig as structural Verilog
module cpu (
  input  clk
);

  wire controlunit_1_flagwrite, controlunit_1_memread, controlunit_1_memwrite, controlunit_1_pcsource,
       controlunit_1_regwrite, minialu_1_zero_flag;
  wire [1:0] controlunit_1_regwritesource;
  wire [3:0] DataRam_d, minialu_1_result, mux_1_out, programrom_1_d, registerfile_1_da, registerfile_1_db;
  wire [5:0] add_1_s, multiplexer_1_out, programcounter_1_out;
  wire [13:4] programrom_1_d_2;

  // Probe on multiplexer_1_out
  programCounter programcounter_1 (.C(clk), .Id(clk), .clr(1'b0), .in(multiplexer_1_out), .out(programcounter_1_out));
  // Probe on programcounter_1_out
  Add #(.Bits(6)) add_1 (.a(programcounter_1_out), .b(6'b000001), .c_i(1'b0), .s(add_1_s));  // open: c_o
  programROM programrom_1 (.A(programcounter_1_out), .D({programrom_1_d_2, programrom_1_d}));
  controlUnit controlunit_1 (
    .Opcode(programrom_1_d_2[13:11]), .Type_bit(programrom_1_d_2[10]), .Zero_Flag(minialu_1_zero_flag),
    .RegWrite(controlunit_1_regwrite), .MemRead(controlunit_1_memread), .MemWrite(controlunit_1_memwrite),
    .FlagWrite(controlunit_1_flagwrite), .PCSource(controlunit_1_pcsource),
    .RegWriteSource(controlunit_1_regwritesource));
  Multiplexer #(.Bits(6)) multiplexer_1 (
    .sel(controlunit_1_pcsource), .in_0(add_1_s), .in_1({2'b00, programrom_1_d}), .out(multiplexer_1_out));
  // Probe on programrom_1_d_2[13:11]
  // Probe on programrom_1_d
  // Probe on programrom_1_d_2[10]
  // Probe on controlunit_1_memwrite
  registerFile registerfile_1 (
    .Din(mux_1_out), .we(controlunit_1_regwrite), .Rw(programrom_1_d_2[9:7]), .C(clk),
    .Ra(programrom_1_d_2[9:7]), .Rb(programrom_1_d_2[6:4]), .Da(registerfile_1_da), .Db(registerfile_1_db));
  // Probe on registerfile_1_da
  // Probe on controlunit_1_memread
  // Probe on registerfile_1_da
  // Probe on registerfile_1_db
  // Probe on {2'b00, programrom_1_d}
  EEPROMDualPort #(.AddrBits(6), .Bits(4)) DataRam (
    .A({2'b00, programrom_1_d}), .Din(registerfile_1_da), .str(controlunit_1_memwrite), .C(clk),
    .ld(controlunit_1_memread), .D(DataRam_d));
  miniALU minialu_1 (
    .A(registerfile_1_da), .B(registerfile_1_db), .FlagWrite(controlunit_1_flagwrite), .Clock(clk),
    .Result(minialu_1_result), .Zero_flag(minialu_1_zero_flag));
  // Probe on minialu_1_result
  Mux mux_1 (
    .in_0(minialu_1_result), .in_1(DataRam_d), .in_2(registerfile_1_db), .in_3(4'b0000),
    .sel(controlunit_1_regwritesource), .out(mux_1_out));

  // Notes on the sheet:
  //   Reg2_Addr
  //   Reg1_Addr
  //   Type_Bit
  //   Opcode
  //   PCSource
  //   Address_Field
  //   Address_Field_Ext
  //   contents of DataRam (hex, n*v repeats v):
  //   a,0,4,f
  //   RegWriteSource
endmodule
