// Digital circuit miniALU.dig as structural Verilog
module miniALU (
  input  [3:0] A,
  input  [3:0] B,
  input  FlagWrite,
  input  Clock,
  output [3:0] Result,
  output Zero_flag
);

  wire nor_1_out;

  rcAdder rcadder_1 (.Ci(1'b0), .A(A), .B(B), .Result(Result));  // open: Co
  nor nor_1 (nor_1_out, Result[0], Result[1], Result[2], Result[3]);
  Register register_1 (.D(nor_1_out), .C(Clock), .en(FlagWrite), .Q(Zero_flag));
endmodule
