// Digital circuit programCounter.dig as structural Verilog
module programCounter (
  input  C,
  input  Id,
  input  clr,
  input  [5:0] in,
  output [5:0] out
);

  CounterPreset #(.Bits(6)) counterpreset_1 (
    .en(1'b1), .C(C), .dir(1'b0), .in(in), .ld(Id), .clr(clr), .out(out));  // open: ovf
endmodule
