// Digital circuit programROM.dig as structural Verilog
module programROM (
  input  [5:0] A,
  output [13:0] D
);

  ROM #(.AddrBits(6), .Bits(14)) rom_1 (.A(A), .sel(1'b1), .D(D));

  // Notes on the sheet:
  //   contents of rom_1 (hex, n*v repeats v):
  //   482,110,10a0,882,2000
endmodule
