// Digital circuit registerFile.dig as structural Verilog
module registerFile (
  input  [3:0] Din,
  input  we,
  input  [2:0] Rw,
  input  C,
  input  [2:0] Ra,
  input  [2:0] Rb,
  output [3:0] Da,
  output [3:0] Db
);

  RegisterFile #(.AddrBits(3), .Bits(4)) registerfile_1 (
    .Din(Din), .we(we), .Rw(Rw), .C(C), .Ra(Ra), .Rb(Rb), .Da(Da), .Db(Db));
endmodule
