// Digital circuit controlUnit.dig as structural Verilog
module controlUnit (
  input  [2:0] Opcode,
  input  Type_bit,
  input  Zero_Flag,
  output RegWrite,
  output MemRead,
  output MemWrite,
  output FlagWrite,
  output PCSource,
  output [1:0] RegWriteSource,
  output ALUSub
);

  wire and_1_out, and_2_out, decoder_1_out_0, decoder_1_out_3, decoder_1_out_4, decoder_1_out_5, not_1_out;

  Decoder #(.Selector_Bits(3)) decoder_1 (
    .sel(Opcode), .out_0(decoder_1_out_0), .out_1(MemWrite), .out_2(FlagWrite), .out_3(decoder_1_out_3),
    .out_4(decoder_1_out_4), .out_5(decoder_1_out_5));  // open: out_6, out_7
  not not_1 (not_1_out, Type_bit);
  and and_1 (and_1_out, decoder_1_out_3, Zero_Flag);
  and and_2 (and_2_out, decoder_1_out_0, not_1_out);
  and and_3 (MemRead, Type_bit, decoder_1_out_0);
  or or_1 (PCSource, decoder_1_out_4, and_1_out);
  or or_2 (RegWriteSource[0], MemRead, decoder_1_out_5);
  or or_3 (RegWrite, decoder_1_out_0, decoder_1_out_5, FlagWrite);
  or or_4 (RegWriteSource[1], and_2_out, decoder_1_out_5);
  and and_4 (ALUSub, Type_bit, FlagWrite);

  // Notes on the sheet:
  //   LDI
  //   LOAD
  //   Store
  //   ADD
  //   BZ
  //   BR
  //   sel0
  //   sel1
endmodule

/* Test case tt:
Opcode Type_bit Zero_Flag RegWrite MemRead MemWrite FlagWrite PCSource RegWriteSource ALUSub
0b000 0 0 1 0 0 0 0 0b10 0
0b000 1 0 1 1 0 0 0 0b01 0
0b001 0 0 0 0 1 0 0 0b00 0
0b010 0 0 1 0 0 1 0 0b00 0
0b010 1 0 1 0 0 1 0 0b00 1
0b011 0 0 0 0 0 0 0 0b00 0
0b011 0 1 0 0 0 0 1 0b00 0
0b100 0 0 0 0 0 0 1 0b00 0
0b100 0 1 0 0 0 0 1 0b00 0
0b101 0 0 1 0 0 0 0 0b11 0
0b101 1 0 1 0 0 0 0 0b11 0
0b110 0 0 0 0 0 0 0 0b00 0
0b111 0 0 0 0 0 0 0 0b00 0
*/
