// Digital circuit cpu.dig as structural Verilog
module cpu (
  input  clk,
  input  SW3,
  input  SW2,
  input  SW1,
  input  SW0,
  output IO_High,
  output DispSel,
  output SwSel,
  output DispWrite,
  output [3:0] DispValue,
  output [3:0] SW,
  output [3:0] MemOrSwData
);

  wire controlunit_1_alusub, controlunit_1_flagwrite, controlunit_1_memread, controlunit_1_memwrite,
       controlunit_1_pcsource, controlunit_1_regwrite, minialu_1_zero_flag, not_1_out;
  wire [1:0] controlunit_1_regwritesource;
  wire [3:0] DataRam_d, minialu_1_result, mux_1_out, programrom_1_d, registerfile_1_da, registerfile_1_db;
  wire [5:0] add_1_s, multiplexer_1_out, programcounter_1_out;
  wire [6:0] rom_1_d;
  wire [13:4] programrom_1_d_2;

  // Probe on multiplexer_1_out
  ROM #(.AddrBits(4), .Bits(7)) rom_1 (.A(DispValue), .sel(1'b1), .D(rom_1_d));
  programCounter programcounter_1 (.C(clk), .Id(clk), .clr(1'b0), .in(multiplexer_1_out), .out(programcounter_1_out));
  // Probe on programcounter_1_out
  Add #(.Bits(6)) add_1 (.a(programcounter_1_out), .b(6'b000001), .c_i(1'b0), .s(add_1_s));  // open: c_o
  programROM programrom_1 (.A(programcounter_1_out), .D({programrom_1_d_2, programrom_1_d}));
  controlUnit controlunit_1 (
    .Opcode(programrom_1_d_2[13:11]), .Type_bit(programrom_1_d_2[10]), .Zero_Flag(minialu_1_zero_flag),
    .RegWrite(controlunit_1_regwrite), .MemRead(controlunit_1_memread), .MemWrite(controlunit_1_memwrite),
    .FlagWrite(controlunit_1_flagwrite), .PCSource(controlunit_1_pcsource),
    .RegWriteSource(controlunit_1_regwritesource), .ALUSub(controlunit_1_alusub));
  Multiplexer #(.Bits(6)) multiplexer_1 (
    .sel(controlunit_1_pcsource), .in_0(add_1_s), .in_1({2'b00, programrom_1_d}), .out(multiplexer_1_out));
  // Probe on programrom_1_d_2[13:11]
  // Probe on programrom_1_d_2[10]
  Seven_Seg seven_seg_1 (
    .a(rom_1_d[0]), .b(rom_1_d[1]), .c(rom_1_d[2]), .d(rom_1_d[3]), .e(rom_1_d[4]), .f(rom_1_d[5]),
    .g(rom_1_d[6]), .dp(1'b0));
  not not_1 (not_1_out, programrom_1_d[0]);
  and and_1 (SwSel, programrom_1_d[0], IO_High);
  // Probe on controlunit_1_memwrite
  registerFile registerfile_1 (
    .Din(mux_1_out), .we(controlunit_1_regwrite), .Rw(programrom_1_d_2[9:7]), .C(clk),
    .Ra(programrom_1_d_2[9:7]), .Rb(programrom_1_d_2[6:4]), .Da(registerfile_1_da), .Db(registerfile_1_db));
  and and_2 (IO_High, programrom_1_d[1], programrom_1_d[2], programrom_1_d[3]);
  // Probe on registerfile_1_da
  // Probe on controlunit_1_memread
  // Probe on {2'b00, programrom_1_d}
  EEPROMDualPort #(.AddrBits(6), .Bits(4)) DataRam (
    .A({2'b00, programrom_1_d}), .Din(registerfile_1_da), .str(controlunit_1_memwrite), .C(clk),
    .ld(controlunit_1_memread), .D(DataRam_d));
  miniALU minialu_1 (
    .A(registerfile_1_da), .B(registerfile_1_db), .FlagWrite(controlunit_1_flagwrite), .Clock(clk),
    .Sub(controlunit_1_alusub), .Result(minialu_1_result), .Zero_flag(minialu_1_zero_flag));
  // Probe on minialu_1_result
  Multiplexer #(.Bits(4)) multiplexer_2 (.sel(SwSel), .in_0(DataRam_d), .in_1({SW0, SW1, SW2, SW3}), .out(MemOrSwData));
  Mux mux_1 (
    .in_0(minialu_1_result), .in_1(MemOrSwData), .in_2(registerfile_1_db), .in_3(programrom_1_d),
    .sel(controlunit_1_regwritesource), .out(mux_1_out));
  and and_3 (DispSel, not_1_out, IO_High);
  and and_4 (DispWrite, DispSel, controlunit_1_memwrite);
  Register #(.Bits(4)) register_1 (.D(registerfile_1_da), .C(clk), .en(DispWrite), .Q(DispValue));
  Seven_Seg_Hex seven_seg_hex_1 (.d(DispValue), .dp(1'b0));

  assign SW = {SW0, SW1, SW2, SW3};

  // Notes on the sheet:
  //   contents of rom_1 (hex, n*v repeats v):
  //   3f,6,5b,4f,66,6d,7d,7,7f,6f,77,7c,39,5e,79,71
  //   Reg2_Addr
  //   Reg1_Addr
  //   Type_Bit
  //   Opcode
  //   PCSource
  //   Address_Field
  //   Address_Field_Ext
  //   NOT_A0
  //   contents of DataRam (hex, n*v repeats v):
  //   a,0,4,f
  //   RegWriteSource
endmodule
