// Digital circuit fullAdder.dig as structural Verilog
module fullAdder (
  input  Ci,
  input  A,
  input  B,
  output Co,
  output S
);

  wire halfadder_1_c, halfadder_1_s, halfadder_2_c;

  halfAdder halfadder_1 (.A(A), .B(B), .S(halfadder_1_s), .C(halfadder_1_c));
  halfAdder halfadder_2 (.A(Ci), .B(halfadder_1_s), .S(S), .C(halfadder_2_c));
  or or_1 (Co, halfadder_2_c, halfadder_1_c);
endmodule
