// Digital circuit miniALU.dig as structural Verilog
module miniALU (
  input  [3:0] A,
  input  [3:0] B,
  input  FlagWrite,
  input  Clock,
  input  Sub,
  output [3:0] Result,
  output Zero_flag
);

  wire nor_1_out;
  wire [3:0] multiplexer_1_out, not_1_out;

  rcAdder rcadder_1 (.Ci(Sub), .A(A), .B(multiplexer_1_out), .Result(Result));  // open: Co
  assign not_1_out = ~B;  // Not not_1, 4 bits wide
  nor nor_1 (nor_1_out, Result[0], Result[1], Result[2], Result[3]);
  Multiplexer #(.Bits(4)) multiplexer_1 (.sel(Sub), .in_0(B), .in_1(not_1_out), .out(multiplexer_1_out));
  Register register_1 (.D(nor_1_out), .C(Clock), .en(FlagWrite), .Q(Zero_flag));
endmodule
