// Digital circuit programROM.dig as structural Verilog
module programROM (
  input  [5:0] A,
  output [13:0] D
);

  ROM #(.AddrBits(6), .Bits(14)) rom_1 (.A(A), .sel(1'b1), .D(D));

  // Notes on the sheet:
  //   contents of rom_1 (hex, n*v repeats v):
  //   48f,2901,2980,10b0,1808,88e,14a0,2003,88e,2009
endmodule
