// Digital circuit rcAdder.dig as structural Verilog
module rcAdder (
  input  Ci,
  input  [3:0] A,
  input  [3:0] B,
  output [3:0] Result,
  output Co
);

  wire fulladder_1_p4, fulladder_2_p4, fulladder_3_p4;

  // fullAdder fulladder_1: pin names not known; wires that end beside it: Ci, A[0], B[0], fulladder_1_p4, Result[0]
  // fullAdder fulladder_2: pin names not known; wires that end beside it: fulladder_1_p4, A[1], B[1], fulladder_2_p4, Result[1]
  // fullAdder fulladder_3: pin names not known; wires that end beside it: fulladder_2_p4, A[2], B[2], fulladder_3_p4, Result[2]
  // fullAdder fulladder_4: pin names not known; wires that end beside it: fulladder_3_p4, A[3], B[3], Co, Result[3]
endmodule

/* Test case:
 A B Ci S Co
 0 0 0 0 0 
 1 1 0 2 0 
 15 1 0 0 1 
 5 11 0 0 1 
 7 0 1 8 0 
 15 15 1 15 1 
*/
