// Digital circuit controlUnit.dig as structural Verilog
module controlUnit (
  input  [2:0] Opcode,
  input  Type_bit,
  input  Zero_Flag,
  output RegWrite,
  output MemRead,
  output MemWrite,
  output FlagWrite,
  output [1:0] PCSource,
  output [1:0] RegWriteSource,
  output ALUSub,
  output TxZ,
  output StackOp,
  output Push,
  output POP,
  output StackRead,
  output DinSel
);

  wire and_1_out, and_2_out, and_3_out, and_10_out, decoder_1_out_0, decoder_1_out_1, decoder_1_out_3,
       decoder_1_out_4, decoder_1_out_5, decoder_1_out_6, decoder_1_out_7, not_1_out;

  Decoder #(.Selector_Bits(3)) decoder_1 (
    .sel(Opcode), .out_0(decoder_1_out_0), .out_1(decoder_1_out_1), .out_2(FlagWrite),
    .out_3(decoder_1_out_3), .out_4(decoder_1_out_4), .out_5(decoder_1_out_5), .out_6(decoder_1_out_6),
    .out_7(decoder_1_out_7));
  not not_1 (not_1_out, Type_bit);
  and and_1 (and_1_out, decoder_1_out_3, TxZ);
  or or_1 (StackOp, decoder_1_out_6, decoder_1_out_7);
  and and_2 (and_2_out, decoder_1_out_0, not_1_out);
  and and_3 (and_3_out, Type_bit, decoder_1_out_0);
  // Or or_2 has open pins: In_1=decoder_1_out_4, In_2=and_1_out, out=open
  and and_4 (Push, StackOp, not_1_out);
  and and_5 (POP, decoder_1_out_6, Type_bit);
  and and_6 (DinSel, decoder_1_out_7, not_1_out);
  and and_7 (PCSource[1], decoder_1_out_7, Type_bit);
  xor xor_1 (TxZ, Type_bit, Zero_Flag);
  or or_3 (RegWriteSource[0], and_3_out, decoder_1_out_5, POP);
  and and_8 (StackRead, StackOp, Type_bit);
  or or_4 (RegWriteSource[1], and_2_out, decoder_1_out_5);
  or or_5 (RegWrite, decoder_1_out_0, decoder_1_out_5, FlagWrite, POP);
  and and_9 (ALUSub, Type_bit, FlagWrite);
  or or_6 (MemRead, and_3_out, StackRead);
  or or_7 (MemWrite, decoder_1_out_1, Push);
  and and_10 (and_10_out, TxZ, decoder_1_out_3);
  or or_8 (PCSource[0], decoder_1_out_4, and_10_out, DinSel);

  // Notes on the sheet:
  //   CR
  //   PP
  //   LDI
  //   LOAD
  //   Store
  //   ADD
  //   BZ
  //   BR
  //   RET
  //   sel0
  //   sel1
  //   Taken
  //   PC0
endmodule

/* Test case tt:
Opcode Type_bit Zero_Flag RegWrite MemRead MemWrite FlagWrite PCSource RegWriteSource ALUSub
0b000 0 0 1 0 0 0 0 0b10 0
0b000 1 0 1 1 0 0 0 0b01 0
0b001 0 0 0 0 1 0 0 0b00 0
0b010 0 0 1 0 0 1 0 0b00 0
0b010 1 0 1 0 0 1 0 0b00 1
0b011 0 0 0 0 0 0 0 0b00 0
0b011 0 1 0 0 0 0 1 0b00 0
0b011 1 0 0 0 0 0 1 0b00 0
0b011 1 1 0 0 0 0 0 0b00 0
0b100 0 0 0 0 0 0 1 0b00 0
0b100 0 1 0 0 0 0 1 0b00 0
0b101 0 0 1 0 0 0 0 0b11 0
0b101 1 0 1 0 0 0 0 0b11 0
*/

/* Test case Call:
Opcode Type_bit Zero_Flag PCSource DinSel StackOp Push MemWrite MemRead
0b111 0 0 0b01 1 1 1 1 0
0b111 0 1 0b01 1 1 1 1 0
0b111 1 0 0b10 0 1 0 0 1
0b111 1 1 0b10 0 1 0 0 1
0b100 0 0 0b01 0 0 0 0 0
0b110 0 0 0b00 0 1 1 1 0
*/

/* Test case Stack:
Opcode Type_bit Zero_Flag RegWrite MemRead MemWrite RegWriteSource StackOp Push
0b110 0 0 0 0 1 0b00 1 1
0b110 1 0 1 1 0 0b01 1 0
0b111 0 0 0 0 1 0b00 1 1
0b111 1 0 0 1 0 0b00 1 0
0b000 1 0 1 1 0 0b01 0 0
*/
