// Digital circuit dataRAM.dig as structural Verilog
module dataRAM (
  input  [5:0] A,
  input  [3:0] Din,
  input  str,
  input  C,
  input  ld,
  output [3:0] D
);

  EEPROMDualPort #(.AddrBits(6), .Bits(4)) eepromdualport_1 (.A(A), .Din(Din), .str(str), .C(C), .ld(ld), .D(D));
  // Probe on D

  // Notes on the sheet:
  //   contents of eepromdualport_1 (hex, n*v repeats v):
  //   0,0,5,6*0,a
endmodule
