// Digital circuit programROM.dig as structural Verilog
module programROM (
  input  [5:0] A,
  output [13:0] D
);

  ROM #(.AddrBits(6), .Bits(14)) rom_1 (.A(A), .sel(1'b1), .D(D));

  // Notes on the sheet:
  //   contents of rom_1 (hex, n*v repeats v):
  //   48f,2909,3807,3809,1c03,90d,2006,88e,3c00,3100,2901,14a0,3807
  //   ,3500,3c00
endmodule
