// Digital circuit Mux.dig as structural Verilog
module Mux (
  input  [3:0] in_0,
  input  [3:0] in_1,
  input  [3:0] in_2,
  input  [3:0] in_3,
  input  [1:0] sel,
  output [3:0] out
);

  Multiplexer #(.Bits(4), .Selector_Bits(2)) multiplexer_1 (
    .sel(sel), .in_0(in_0), .in_1(in_1), .in_2(in_2), .in_3(in_3), .out(out));
endmodule
