// Digital circuit dataRam.dig as structural Verilog
module dataRam (
  input  [5:0] A,
  input  [3:0] Din,
  input  str,
  input  ld,
  input  C,
  output [3:0] D
);

  EEPROMDualPort #(.AddrBits(6), .Bits(4)) eepromdualport_1 (.A(A), .Din(Din), .str(str), .C(C), .ld(ld), .D(D));
endmodule
