// Digital circuit fullAdder.dig as structural Verilog
module fullAdder (
  input  A,
  input  B,
  input  CIN,
  output SUM,
  output COUT
);

  wire halfadder_1_carry, halfadder_1_sum, halfadder_2_carry;

  halfAdder halfadder_1 (.A(A), .B(B), .SUM(halfadder_1_sum), .CARRY(halfadder_1_carry));
  halfAdder halfadder_2 (.A(halfadder_1_sum), .B(CIN), .SUM(SUM), .CARRY(halfadder_2_carry));
  or or_1 (COUT, halfadder_1_carry, halfadder_2_carry);
endmodule
