// Digital circuit miniALU.dig as structural Verilog
module miniALU (
  input  [3:0] A,
  input  [3:0] B,
  input  FlagWrite,
  input  Clock,
  output Zero_Flag
);

  wire nor_1_out;
  wire [3:0] rcadder_1_result;

  rcAdder rcadder_1 (.A(A), .B(B), .Result(rcadder_1_result));  // open: Co
  nor nor_1 (nor_1_out, rcadder_1_result[0], rcadder_1_result[1], rcadder_1_result[2], rcadder_1_result[3]);
  Register register_1 (.D(nor_1_out), .C(Clock), .en(FlagWrite), .Q(Zero_Flag));
endmodule
