// Digital circuit rcAdder.dig as structural Verilog
module rcAdder (
  input  [3:0] A,
  input  [3:0] B,
  output Co,
  output [3:0] Result
);

  wire fulladder_1_p5, fulladder_2_p5, fulladder_3_p5;

  // fullAdder fulladder_1: pin names not known; wires that end beside it: A[0], B[0], 1'b0, Result[0], fulladder_1_p5
  // fullAdder fulladder_2: pin names not known; wires that end beside it: A[1], B[1], fulladder_1_p5, Result[1], fulladder_2_p5
  // fullAdder fulladder_3: pin names not known; wires that end beside it: A[2], B[2], fulladder_2_p5, Result[2], fulladder_3_p5
  // fullAdder fulladder_4: pin names not known; wires that end beside it: A[3], B[3], fulladder_3_p5, Result[3], Co
endmodule

/* Test case:
A B Result Co
0 0 0 0
1 1 2 0
3 2 5 0
5 3 8 0
7 1 8 0
15 1 0 1
8 8 0 1
15 15 14 1
10 3 13 0
12 4 0 1
*/
